// Logisim project ALU.circ as structural Verilog: 4 circuits, main circuit ALU
module ALU (
  input  [31:0] A,
  input  [31:0] B,
  input  [4:0] Shift,
  input  [3:0] Codop,
  input  CarryIn,
  output [31:0] S,
  output [3:0] Flags
);

  wire AND1, AND2, AND3, AND4, and_4_out, and_5_out, and_6_out, and_7_out, CarryOut_ADC, CarryOut_ASR,
       CarryOut_CMN, CarryOut_CMP, CarryOut_LSL, CarryOut_RSB, CarryOut_SBC, comparator_1_gt,
       comparator_1_lt, isADC, isArith, isCMN, isCMP, isRSB, isSBC, isSub, not_1_out, not_6_out, not_7_out,
       not_8_out, not_9_out, not_10_out, not_11_out, subtractor_1_bout, subtractor_2_bout, V, V_add, V_RSB,
       V_sub;
  wire [4:0] negator_1_out, subtractor_3_out;
  wire [31:0] ADD, ADDCIN, BETNONA, DECD, DECDA, DECDR, DECG, ET, MULT, NONA, not_4_out, NOU, OU, RSB, SBC,
       SOUS, TST;

  Adder #(.width(32)) adder_1 (.a(A), .b(B), .out(ADD), .cout(CarryOut_CMN));  // open: cin
  Comparator #(.width(32)) comparator_1 (
    .a({32{1'b0}}), .b(A), .gt(comparator_1_gt), .lt(comparator_1_lt));  // open: eq
  not not_1 (not_1_out, CarryIn);
  Subtractor #(.width(32)) subtractor_1 (.a(B), .b(A), .out(SBC), .bin(not_1_out), .bout(subtractor_1_bout));
  BitSelector #(.width(32)) bitselector_1 (.in(B), .out(CarryOut_LSL), .sel(negator_1_out));
  Negator #(.width(5)) negator_1 (.in(Shift), .out(negator_1_out));
  not not_2 (CarryOut_CMP, subtractor_2_bout);
  not not_3 (CarryOut_SBC, subtractor_1_bout);
  nor nor_1 (CarryOut_RSB, comparator_1_gt, comparator_1_lt);
  Subtractor #(.width(32)) subtractor_2 (.a(B), .b(A), .out(SOUS), .bout(subtractor_2_bout));  // open: bin
  Adder #(.width(32)) adder_2 (.a(A), .b(B), .out(ADDCIN), .cin(CarryIn), .cout(CarryOut_ADC));
  Multiplier #(.width(32)) multiplier_1 (.a(A), .b(B), .out(MULT));  // open: cin, cout
  BitSelector #(.width(32)) bitselector_2 (.in(B), .out(CarryOut_ASR), .sel(subtractor_3_out));
  Subtractor #(.width(5)) subtractor_3 (.a(Shift), .b(5'b00001), .out(subtractor_3_out));  // open: bin, bout
  assign not_4_out = ~A;  // NOT_Gate not_4, 32 bits wide
  or or_1 (isArith, isADC, isRSB, isCMP, isSBC, isCMN);
  Multiplexer #(.select(4), .width(32)) multiplexer_1 (
    .in0(ET), .in1(NOU), .in2(DECG), .in3(DECD), .in4(DECDA), .in5(ADDCIN), .in6(SBC), .in7(DECDR), .in8(A),
    .in9(RSB), .in10(SOUS), .in11(ADD), .in12(OU), .in13(MULT), .in14(BETNONA), .in15(NONA),
    .out({Flags[3], S[30:0]}), .sel(Codop));
  assign ET = A & B;  // AND_Gate and_1, 32 bits wide
  assign NOU = A ^ B;  // XOR_Gate xor_1, 32 bits wide
  assign NONA = ~A;  // NOT_Gate not_5, 32 bits wide
  assign BETNONA = B & not_4_out;  // AND_Gate and_2, 32 bits wide
  Shifter #(.shift("lr"), .width(32)) shifter_1 (.in(B), .\dist (Shift), .out(DECD));
  Comparator #(.width(32)) comparator_2 (.a({Flags[3], S[30:0]}), .b({32{1'b0}}), .eq(Flags[2]));  // open: gt, lt
  Shifter #(.shift("rr"), .width(32)) shifter_2 (.in(B), .\dist (Shift), .out(DECDR));
  Subtractor #(.width(32)) subtractor_4 (.a({32{1'b0}}), .b(A), .out(RSB));  // open: bin, bout
  Multiplexer multiplexer_2 (.in0(1'b0), .in1(V), .out(Flags[0]), .sel(isArith));
  assign OU = A | B;  // OR_Gate or_2, 32 bits wide
  assign TST = A & B;  // AND_Gate and_3, 32 bits wide
  Shifter #(.width(32)) shifter_3 (.in(B), .\dist (Shift), .out(DECG));
  Shifter #(.shift("ar"), .width(32)) shifter_4 (.in(B), .\dist (Shift), .out(DECDA));
  Shifter #(.shift("rr"), .width(32)) shifter_5 (.in(B), .\dist (Shift), .out(DECDR));
  Multiplexer #(.select(4)) multiplexer_3 (
    .in0(1'b0), .in1(1'b0), .in2(CarryOut_LSL), .in3(CarryOut_ASR), .in4(CarryOut_ASR), .in5(CarryOut_ADC),
    .in6(CarryOut_SBC), .in7(DECDR[31]), .in8(1'b0), .in9(1'b0), .in10(CarryOut_CMP), .in11(CarryOut_CMN),
    .in12(1'b0), .in13(1'b0), .in14(1'b0), .in15(1'b0), .out(Flags[1]), .sel(Codop));
  Multiplexer #(.select(4)) multiplexer_4 (
    .in0(1'b0), .in1(1'b0), .in2(1'b0), .in3(1'b0), .in4(1'b0), .in5(V_add), .in6(V_sub), .in7(1'b0),
    .in8(1'b0), .in9(V_RSB), .in10(V_sub), .in11(V_add), .in12(1'b0), .in13(1'b0), .in14(1'b0), .in15(1'b0),
    .out(V), .sel(Codop));
  not not_6 (not_6_out, A[31]);
  Comparator #(.width(4)) comparator_3 (.a(Codop), .b(4'b0101), .eq(isADC));  // open: gt, lt
  Comparator #(.width(4)) comparator_4 (.a(Codop), .b(4'b1001), .eq(isRSB));  // open: gt, lt
  Comparator #(.width(4)) comparator_5 (.a(Codop), .b(4'b1010), .eq(isCMP));  // open: gt, lt
  Comparator #(.width(4)) comparator_6 (.a(Codop), .b(4'b0110), .eq(isSBC));  // open: gt, lt
  Comparator #(.width(4)) comparator_7 (.a(Codop), .b(4'b1011), .eq(isCMN));  // open: gt, lt
  not not_7 (not_7_out, A[31]);
  not not_8 (not_8_out, B[31]);
  not not_9 (not_9_out, B[31]);
  and and_4 (and_4_out, A[31], B[31]);
  not not_10 (not_10_out, ADD[31]);
  and and_5 (and_5_out, not_7_out, not_8_out);
  and and_6 (and_6_out, B[31], not_6_out);
  not not_11 (not_11_out, SOUS[31]);
  and and_7 (and_7_out, not_9_out, A[31]);
  and and_8 (AND1, and_4_out, not_10_out);
  and and_9 (AND2, and_5_out, ADD[31]);
  or or_3 (V_add, AND1, AND2);
  and and_10 (AND3, and_6_out, not_11_out);
  and and_11 (AND4, and_7_out, SOUS[31]);
  or or_4 (V_sub, AND3, AND4);
  Multiplexer #(.select(4)) multiplexer_5 (
    .in0(1'b0), .in1(1'b0), .in2(1'b0), .in3(1'b0), .in4(1'b0), .in5(1'b1), .in6(1'b1), .in7(1'b0),
    .in8(1'b0), .in9(1'b0), .in10(1'b1), .in11(1'b1), .in12(1'b0), .in13(1'b0), .in14(1'b0), .in15(1'b0),
    .out(isSub), .sel(Codop));
  and and_12 (V_RSB, A[31], RSB[31]);

  assign S[31] = Flags[3];

  // Other names for the same wires on the sheet: Sadd31 = ADD[31]; CarryOut_LSR = CarryOut_ASR; Cin = CarryIn;
  //   V_final = Flags[0]; COUT = Flags[1]; Z = Flags[2]; Srsb31 = RSB[31]; N = Flags[3]; Ssous31 = SOUS[31]

  // Notes on the sheet:
  //   Note: for ROR, C = N
  //   Note 2: assume that shift > 0 for LSL and LSR
endmodule

module Control_instruction (
  input  [15:0] INST
);

  wire and_1_out, and_2_out, and_3_out, and_4_out, and_5_out, and_6_out, and_7_out, and_8_out, isADD, isCMP,
       isMOV, isSUB, not_1_out, not_2_out, not_3_out, not_4_out, not_5_out, not_6_out, not_7_out, not_8_out,
       not_9_out, op0, op1;

  not not_1 (not_1_out, INST[13]);
  not not_2 (not_2_out, INST[13]);
  not not_3 (not_3_out, INST[12]);
  not not_4 (not_4_out, INST[12]);
  and and_1 (and_1_out, INST[12], not_1_out);
  and and_2 (and_2_out, INST[13], INST[12]);
  and and_3 (and_3_out, not_2_out, not_3_out);
  and and_4 (and_4_out, INST[13], not_4_out);
  not not_5 (not_5_out, op1);
  not not_6 (not_6_out, op1);
  and and_5 (and_5_out, and_1_out, not_5_out);
  not not_7 (not_7_out, op0);
  and and_6 (and_6_out, and_2_out, not_6_out);
  and and_7 (and_7_out, and_3_out, op1);
  not not_8 (not_8_out, op0);
  and and_8 (and_8_out, and_4_out, op1);
  not not_9 (not_9_out, op0);
  and and_9 (isADD, and_5_out, not_7_out);
  and and_10 (isMOV, and_6_out, op0);
  and and_11 (isSUB, and_7_out, not_8_out);
  and and_12 (isCMP, and_8_out, not_9_out);

  // Other names for the same wires on the sheet: op2 = INST[12]; op3 = INST[13]; op4 = INST[14]; op5 = INST[15]
endmodule

module Control_ShiftAddSubMov (
  input  [15:0] INST
);

  wire isADD;
  wire [15:0] ALU_Opcode;

  Multiplexer #(.width(16)) multiplexer_1 (.in0({16{1'b0}}), .in1(16'h101), .out(ALU_Opcode), .sel(isADD));
endmodule

module OverFlow (
);

  wire A31, B31, isSub, not_1_out, S31, V, V_add, V_sub, xor_1_out, xor_2_out, xor_3_out, xor_4_out;

  xor xor_1 (xor_1_out, A31, S31);
  xor xor_2 (xor_2_out, A31, B31);
  not not_1 (not_1_out, xor_2_out);
  xor xor_3 (xor_3_out, A31, S31);
  xor xor_4 (xor_4_out, A31, B31);
  and and_1 (V_sub, xor_3_out, xor_4_out);
  and and_2 (V_add, xor_1_out, not_1_out);
  Multiplexer multiplexer_1 (.in0(V_add), .in1(V_sub), .out(V), .sel(isSub));
endmodule
