// Logisim project BancDeRegistres.circ as structural Verilog: 1 circuit, main circuit BancRegistre
module BancRegistre (
  input  [2:0] RegA,
  input  [2:0] RegB,
  input  [2:0] RegDest,
  input  [31:0] DataIn,
  input  Clk,
  input  Reset,
  output [31:0] BOut,
  output [31:0] AOut,
  output [31:0] R0,
  output [31:0] R1,
  output [31:0] R2,
  output [31:0] R3,
  output [31:0] R4,
  output [31:0] R5,
  output [31:0] R6,
  output [31:0] R7
);

  wire decoder_1_out0, decoder_1_out1, decoder_1_out2, decoder_1_out3, decoder_1_out4, decoder_1_out5,
       decoder_1_out6, decoder_1_out7, undriven;

  Decoder #(.enable("false"), .select(3)) decoder_1 (
    .out0(decoder_1_out0), .out1(decoder_1_out1), .out2(decoder_1_out2), .out3(decoder_1_out3),
    .out4(decoder_1_out4), .out5(decoder_1_out5), .out6(decoder_1_out6), .out7(decoder_1_out7), .sel(RegDest));
  Register #(.width(32)) Reg0 (.D(DataIn), .en(decoder_1_out0), .clk(undriven), .Q(R0), .clr(Clk));
  Register #(.width(32)) Reg1 (.D(DataIn), .en(decoder_1_out1), .clk(undriven), .Q(R1), .clr(Clk));
  Register #(.width(32)) Reg2 (.D(DataIn), .en(decoder_1_out2), .clk(undriven), .Q(R2), .clr(Clk));
  Register #(.width(32)) Reg3 (.D(DataIn), .en(decoder_1_out3), .clk(undriven), .Q(R1), .clr(Clk));
  Register #(.width(32)) Reg4 (.D(DataIn), .en(decoder_1_out4), .clk(undriven), .Q(R4), .clr(Clk));
  Register #(.width(32)) Reg5 (.D(DataIn), .en(decoder_1_out5), .clk(undriven), .Q(R5), .clr(Clk));
  Register #(.width(32)) Reg6 (.D(DataIn), .en(decoder_1_out6), .clk(undriven), .Q(R6), .clr(Clk));
  Register #(.width(32)) Reg7 (.D(DataIn), .en(decoder_1_out7), .clk(undriven), .Q(R7), .clr(Clk));
  Multiplexer #(.select(3), .width(32)) multiplexer_1 (
    .in0(R0), .in1(R1), .in2(R2), .in3(R1), .in4(R4), .in5(R5), .in6(R6), .in7(R7), .out(AOut), .sel(RegA));
  Multiplexer #(.select(3), .width(32)) multiplexer_2 (
    .in0(R0), .in1(R1), .in2(R2), .in3(R1), .in4(R4), .in5(R5), .in6(R6), .in7(R7), .out(BOut), .sel(RegB));

  assign R3 = R1;

  // Other names for the same wires on the sheet: Clock = Clk
endmodule
