// Logisim project Ctl_Conditional.circ as structural Verilog: 1 circuit, main circuit Conditional
module Conditional (
  input  Enable,
  input  [15:0] Instruction,
  input  Z,
  input  C,
  input  N,
  input  V,
  output [10:0] Offset,
  output Verified
);

  wire AL_OK, and_1_out, and_2_out, B_UNCOUND, CC_OK, comparator_1_eq, comparator_2_eq, comparator_3_eq,
       comparator_4_eq, comparator_5_eq, comparator_6_eq, comparator_8_eq, comparator_9_eq, comparator_10_eq,
       comparator_11_eq, comparator_12_eq, comparator_13_eq, comparator_14_eq, comparator_15_eq, cond_true,
       CS_OK, EQ_OK, GE_OK, GT_OK, HI_OK, LE_OK, LS_OK, LT_OK, MI_OK, NE_OK, not_1_out, not_2_out, not_3_out,
       not_4_out, not_5_out, not_6_out, not_7_out, or_1_out, or_2_out, or_4_out, PL_OK, VC_OK, VS_OK,
       xnor_1_out, xnor_2_out, xor_1_out, xor_2_out;
  wire [10:0] multiplexer_1_out;
  wire [10:8] OFFSET_BC;

  xor xor_1 (xor_1_out, N, V);
  Comparator #(.width(4)) comparator_1 (.a(Instruction[11:8]), .b(4'b0001), .eq(comparator_1_eq));  // open: gt, lt
  not not_1 (not_1_out, Z);
  Comparator #(.width(4)) comparator_2 (.a(Instruction[11:8]), .b(4'b0100), .eq(comparator_2_eq));  // open: gt, lt
  Comparator #(.width(4)) comparator_3 (.a(Instruction[11:8]), .b(4'b0101), .eq(comparator_3_eq));  // open: gt, lt
  Comparator #(.width(4)) comparator_4 (.a(Instruction[11:8]), .b(4'b0110), .eq(comparator_4_eq));  // open: gt, lt
  Comparator #(.width(4)) comparator_5 (.a(Instruction[11:8]), .b(4'b0111), .eq(comparator_5_eq));  // open: gt, lt
  not not_2 (not_2_out, Z);
  and and_1 (and_1_out, not_2_out, C);
  or or_1 (or_1_out, Z, not_3_out);
  not not_3 (not_3_out, C);
  xnor xnor_1 (xnor_1_out, N, V);
  not not_4 (not_4_out, Z);
  and and_2 (and_2_out, not_4_out, xnor_2_out);
  xnor xnor_2 (xnor_2_out, N, V);
  Comparator #(.width(4)) comparator_6 (.a(Instruction[11:8]), .b(4'b1101), .eq(comparator_6_eq));  // open: gt, lt
  or or_2 (or_2_out, Z, xor_1_out);
  Comparator #(.width(4)) comparator_7 (.a(Instruction[11:8]), .b(4'b1110), .eq(AL_OK));  // open: gt, lt
  Comparator #(.width(4)) comparator_8 (.a(Instruction[11:8]), .b(4'b0000), .eq(comparator_8_eq));  // open: gt, lt
  and and_3 (NE_OK, comparator_1_eq, not_1_out);
  Comparator #(.width(4)) comparator_9 (.a(Instruction[11:8]), .b(4'b0010), .eq(comparator_9_eq));  // open: gt, lt
  Comparator #(.width(4)) comparator_10 (.a(Instruction[11:8]), .b(4'b0011), .eq(comparator_10_eq));  // open: gt, lt
  not not_5 (not_5_out, C);
  and and_4 (MI_OK, comparator_2_eq, N);
  and and_5 (PL_OK, comparator_3_eq, not_6_out);
  not not_6 (not_6_out, N);
  and and_6 (VS_OK, comparator_4_eq, V);
  and and_7 (VC_OK, comparator_5_eq, not_7_out);
  not not_7 (not_7_out, V);
  Comparator #(.width(4)) comparator_11 (.a(Instruction[11:8]), .b(4'b1000), .eq(comparator_11_eq));  // open: gt, lt
  Comparator #(.width(4)) comparator_12 (.a(Instruction[11:8]), .b(4'b1001), .eq(comparator_12_eq));  // open: gt, lt
  Comparator #(.width(4)) comparator_13 (.a(Instruction[11:8]), .b(4'b1010), .eq(comparator_13_eq));  // open: gt, lt
  Comparator #(.width(4)) comparator_14 (.a(Instruction[11:8]), .b(4'b1011), .eq(comparator_14_eq));  // open: gt, lt
  and and_8 (LT_OK, comparator_14_eq, xor_2_out);
  xor xor_2 (xor_2_out, N, V);
  Comparator #(.width(4)) comparator_15 (.a(Instruction[11:8]), .b(4'b1100), .eq(comparator_15_eq));  // open: gt, lt
  and and_9 (GT_OK, comparator_15_eq, and_2_out);
  and and_10 (LE_OK, comparator_6_eq, or_2_out);
  Comparator #(.width(5)) comparator_16 (.a(Instruction[15:11]), .b(5'b11100), .eq(B_UNCOUND));  // open: gt, lt
  and and_11 (EQ_OK, comparator_8_eq, Z);
  and and_12 (CS_OK, comparator_9_eq, C);
  and and_13 (CC_OK, comparator_10_eq, not_5_out);
  and and_14 (HI_OK, comparator_11_eq, and_1_out);
  and and_15 (LS_OK, comparator_12_eq, or_1_out);
  and and_16 (GE_OK, comparator_13_eq, xnor_1_out);
  Multiplexer #(.width(11)) multiplexer_1 (
    .in0({OFFSET_BC, Instruction[7:0]}), .in1(Instruction[10:0]), .out(multiplexer_1_out), .sel(B_UNCOUND));
  Multiplexer #(.width(11)) multiplexer_2 (.in0({11{1'b0}}), .in1(multiplexer_1_out), .out(Offset), .sel(Enable));
  or or_3 (cond_true, AL_OK, EQ_OK, NE_OK, CS_OK, CC_OK, MI_OK, PL_OK, VS_OK, VC_OK, HI_OK, LS_OK, GE_OK, LT_OK, GT_OK, LE_OK);
  assign OFFSET_BC = {{2{Instruction[7]}}, Instruction[7]};  // Bit_Extender bit_extender_1
  or or_4 (or_4_out, B_UNCOUND, cond_true);
  and and_17 (Verified, Enable, or_4_out);

  // Other names for the same wires on the sheet: cond[3:0] = Instruction[11:8]; link[7:0] = Instruction[15:8];
  //   OFFSET_B[10:0] = Instruction[10:0]; cond2[4:0] = Instruction[15:11]; imm8[7:0] = Instruction[7:0];
  //   OFFSET_BC[7:0] = Instruction[7:0]
endmodule
