// Logisim project Ctl_Shift_Add_Sub_Mov.circ as structural Verilog: 5 circuits, main circuit Shift_Add_Sub_Mov
module Shift_Add_Sub_Mov (
  input  Enable,
  input  [15:0] Instruction,
  output [3:0] ALU_Opcode,
  output [31:0] Imm32,
  output [2:0] Rm,
  output [2:0] Rn,
  output [2:0] Rd,
  output [4:0] Imm5,
  output [3:0] Flags_Update_Mask,
  output Carry,
  output Imm32_Enable
);

  wire ControlGenn_carry_on, ControlGenn_imm32_enable_on, Decodee_addsub, Decodee_addsub_imm3,
       Decodee_addsub_imm8, Decodee_addsub_reg, Decodee_is_add_any, Decodee_is_asr, Decodee_is_cmp_imm8,
       Decodee_is_imm8_any, Decodee_is_imm_any, Decodee_is_lsl, Decodee_is_lsr, Decodee_is_mov_imm8,
       Decodee_is_shift, Decodee_is_sub_any;
  wire [2:0] ControlGenn_rd_on, ControlGenn_rm_on, ControlGenn_rn_on, ExtractFieldss_imm3_field,
       ExtractFieldss_rd_addsub, ExtractFieldss_rd_mov, ExtractFieldss_rd_shift, ExtractFieldss_rdn,
       ExtractFieldss_rm_addsub, ExtractFieldss_rm_shift, ExtractFieldss_rn_addsub;
  wire [3:0] ControlGenn_alu_opcode_on, ControlGenn_flag_update_mask_on;
  wire [4:0] ControlGenn_imm5_on, ExtractFieldss_imm5_field, ExtractFieldss_op5;
  wire [6:0] ExtractFieldss_op7;
  wire [7:0] ExtractFieldss_imm8_field;
  wire [31:0] ControlGenn_imm32_on;

  ExtractFields ExtractFieldss (
    .Instruction(Instruction), .op5(ExtractFieldss_op5), .op7(ExtractFieldss_op7),
    .imm5_field(ExtractFieldss_imm5_field), .imm3_field(ExtractFieldss_imm3_field),
    .imm8_field(ExtractFieldss_imm8_field), .rm_shift(ExtractFieldss_rm_shift),
    .rd_shift(ExtractFieldss_rd_shift), .rm_addsub(ExtractFieldss_rm_addsub),
    .rn_addsub(ExtractFieldss_rn_addsub), .rd_addsub(ExtractFieldss_rd_addsub),
    .rd_mov(ExtractFieldss_rd_mov), .rdn(ExtractFieldss_rdn));
  Decode Decodee (
    .op5(ExtractFieldss_op5), .op7(ExtractFieldss_op7), .is_shift(Decodee_is_shift),
    .addsub_reg(Decodee_addsub_reg), .addsub_imm3(Decodee_addsub_imm3), .addsub_imm8(Decodee_addsub_imm8),
    .addsub(Decodee_addsub), .is_MOV_imm8(Decodee_is_mov_imm8), .is_imm8_any(Decodee_is_imm8_any),
    .is_imm_any(Decodee_is_imm_any), .is_sub_any(Decodee_is_sub_any), .is_CMP_imm8(Decodee_is_cmp_imm8),
    .is_add_any(Decodee_is_add_any), .is_ASR(Decodee_is_asr), .is_LSR(Decodee_is_lsr), .is_LSL(Decodee_is_lsl));
  ControlGen ControlGenn (
    .is_imm_any(Decodee_is_imm_any), .is_sub_any(Decodee_is_sub_any), .is_shift(Decodee_is_shift),
    .addsub_reg(Decodee_addsub_reg), .addsub_imm3(Decodee_addsub_imm3), .addsub_imm8(Decodee_addsub_imm8),
    .addsub(Decodee_addsub), .is_imm8_any(Decodee_is_imm8_any), .is_CMP_imm8(Decodee_is_cmp_imm8),
    .is_LSL(Decodee_is_lsl), .imm5_field(ExtractFieldss_imm5_field), .imm3_field(ExtractFieldss_imm3_field),
    .imm8_field(ExtractFieldss_imm8_field), .rm_shift(ExtractFieldss_rm_shift),
    .rd_shift(ExtractFieldss_rd_shift), .rdn(ExtractFieldss_rdn), .rm_addsub(ExtractFieldss_rm_addsub),
    .rn_addsub(ExtractFieldss_rn_addsub), .rd_addsub(ExtractFieldss_rd_addsub),
    .rd_mov(ExtractFieldss_rd_mov), .is_MOV_imm8(Decodee_is_mov_imm8), .is_ASR(Decodee_is_asr),
    .is_LSR(Decodee_is_lsr), .is_add_any(Decodee_is_add_any), .ALU_Opcode_On(ControlGenn_alu_opcode_on),
    .Carry_On(ControlGenn_carry_on), .Imm32_Enable_On(ControlGenn_imm32_enable_on),
    .Rn_On(ControlGenn_rn_on), .Imm5_On(ControlGenn_imm5_on), .Imm32_On(ControlGenn_imm32_on),
    .Rm_On(ControlGenn_rm_on), .Flag_Update_Mask_On(ControlGenn_flag_update_mask_on),
    .Rd_On(ControlGenn_rd_on));
  EnableGate EnableGatee (
    .Imm32_Enable_On(ControlGenn_imm32_enable_on), .Imm32_On(ControlGenn_imm32_on),
    .ALU_Opcode_On(ControlGenn_alu_opcode_on), .Rm_On(ControlGenn_rm_on), .Rn_On(ControlGenn_rn_on),
    .Rd_On(ControlGenn_rd_on), .Carry_On(ControlGenn_carry_on), .Imm5_On(ControlGenn_imm5_on),
    .Flag_Update_Mask_On(ControlGenn_flag_update_mask_on), .Enable(Enable), .Imm32(Imm32), .Rn(Rn),
    .ALU_Opcode(ALU_Opcode), .Flag_Update_Mask(Flags_Update_Mask), .Rm(Rm), .Rd(Rd), .Imm5(Imm5),
    .Carry(Carry), .Imm32_Enable(Imm32_Enable));

  // Notes on the sheet:
  //   Note 3: Imm32_Enable forces the use of the immediate for Rm register
  //   Note: ALU uses Rn register for shifts. Use Rn instead of Rm for shifts (immediate) here too
  //   Note 2: MOV uses RSB ALU opcode with Imm8 reversed so that it is copied to output register
  //   Enable carry for SUB since it is reversed in ALU
  //   ALU will use Imm32 instead of Rm
  //   only ADD and SUB use Rm
endmodule

module ExtractFields (
  input  [15:0] Instruction,
  output [4:0] op5,
  output [6:0] op7,
  output [4:0] imm5_field,
  output [2:0] imm3_field,
  output [7:0] imm8_field,
  output [2:0] rm_shift,
  output [2:0] rd_shift,
  output [2:0] rm_addsub,
  output [2:0] rn_addsub,
  output [2:0] rd_addsub,
  output [2:0] rd_mov,
  output [2:0] rdn
);


  assign imm3_field = Instruction[8:6];
  assign imm5_field = Instruction[10:6];
  assign imm8_field = Instruction[7:0];
  assign op5 = Instruction[15:11];
  assign op7 = Instruction[15:9];
  assign rd_addsub = Instruction[2:0];
  assign rd_mov = Instruction[10:8];
  assign rd_shift = Instruction[2:0];
  assign rdn = Instruction[10:8];
  assign rm_addsub = Instruction[8:6];
  assign rm_shift = Instruction[5:3];
  assign rn_addsub = Instruction[5:3];
endmodule

module Decode (
  input  [4:0] op5,
  input  [6:0] op7,
  output is_shift,
  output addsub_reg,
  output addsub_imm3,
  output addsub_imm8,
  output addsub,
  output is_MOV_imm8,
  output is_imm8_any,
  output is_imm_any,
  output is_sub_any,
  output is_CMP_imm8,
  output is_add_any,
  output is_ASR,
  output is_LSR,
  output is_LSL
);

  wire is_ADD_imm3, is_ADD_imm8, is_ADD_reg, is_SUB_imm3, is_SUB_imm8, is_SUB_reg;

  Comparator #(.width(5)) comparator_1 (.a(op5), .b({5{1'b0}}), .eq(is_LSL));  // open: gt, lt
  Comparator #(.width(5)) comparator_2 (.a(op5), .b(5'b00001), .eq(is_LSR));  // open: gt, lt
  Comparator #(.width(5)) comparator_3 (.a(op5), .b(5'b00010), .eq(is_ASR));  // open: gt, lt
  Comparator #(.width(5)) comparator_4 (.a(op5), .b(5'b00100), .eq(is_MOV_imm8));  // open: gt, lt
  Comparator #(.width(5)) comparator_5 (.a(op5), .b(5'b00101), .eq(is_CMP_imm8));  // open: gt, lt
  Comparator #(.width(5)) comparator_6 (.a(op5), .b(5'b00110), .eq(is_ADD_imm8));  // open: gt, lt
  Comparator #(.width(5)) comparator_7 (.a(op5), .b(5'b00111), .eq(is_SUB_imm8));  // open: gt, lt
  Comparator #(.width(7)) comparator_8 (.a(op7), .b(7'b0001100), .eq(is_ADD_reg));  // open: gt, lt
  Comparator #(.width(7)) comparator_9 (.a(op7), .b(7'b0001101), .eq(is_SUB_reg));  // open: gt, lt
  Comparator #(.width(7)) comparator_10 (.a(op7), .b(7'b0001110), .eq(is_ADD_imm3));  // open: gt, lt
  Comparator #(.width(7)) comparator_11 (.a(op7), .b(7'b0001111), .eq(is_SUB_imm3));  // open: gt, lt
  or or_1 (addsub, addsub_reg, addsub_imm3, addsub_imm8);
  or or_2 (is_imm8_any, is_MOV_imm8, is_CMP_imm8, addsub_imm8);
  or or_3 (is_imm_any, is_imm8_any, addsub_imm3);
  or or_4 (is_sub_any, is_SUB_reg, is_SUB_imm8, is_SUB_imm3);
  or or_5 (is_shift, is_ASR, is_LSR, is_LSL);
  or or_6 (addsub_reg, is_ADD_reg, is_SUB_reg);
  or or_7 (addsub_imm3, is_ADD_imm3, is_SUB_imm3);
  or or_8 (addsub_imm8, is_ADD_imm8, is_SUB_imm8);
  or or_9 (is_add_any, is_ADD_reg, is_ADD_imm8, is_ADD_imm3);

  // Other names for the same wires on the sheet: is_addsub = addsub; is_addsub_imm3 = addsub_imm3;
  //   is_addsub_imm8 = addsub_imm8; is_addsub_reg = addsub_reg
endmodule

module ControlGen (
  input  is_imm_any,
  input  is_sub_any,
  input  is_shift,
  input  addsub_reg,
  input  addsub_imm3,
  input  addsub_imm8,
  input  addsub,
  input  is_imm8_any,
  input  is_CMP_imm8,
  input  is_LSL,
  input  [4:0] imm5_field,
  input  [2:0] imm3_field,
  input  [7:0] imm8_field,
  input  [2:0] rm_shift,
  input  [2:0] rd_shift,
  input  [2:0] rdn,
  input  [2:0] rm_addsub,
  input  [2:0] rn_addsub,
  input  [2:0] rd_addsub,
  input  [2:0] rd_mov,
  input  is_MOV_imm8,
  input  is_ASR,
  input  is_LSR,
  input  is_add_any,
  output [3:0] ALU_Opcode_On,
  output Carry_On,
  output Imm32_Enable_On,
  output [2:0] Rn_On,
  output [4:0] Imm5_On,
  output [31:0] Imm32_On,
  output [2:0] Rm_On,
  output [3:0] Flag_Update_Mask_On,
  output [2:0] Rd_On
);

  wire or_1_out, or_2_out, or_3_out;
  wire [2:0] multiplexer_6_out, multiplexer_7_out, multiplexer_9_out, multiplexer_10_out, multiplexer_13_out,
       multiplexer_14_out, multiplexer_15_out, multiplexer_16_out, multiplexer_19_out;
  wire [3:0] m1, m2, m3, multiplexer_1_out, multiplexer_2_out, multiplexer_3_out, multiplexer_5_out,
       multiplexer_8_out, multiplexer_11_out;
  wire [31:0] bit_extender_2_out, imm32_field, multiplexer_20_out, multiplexer_21_out, multiplexer_25_out,
       NEGimm32_field;

  Multiplexer #(.disabled("Z"), .width(4)) multiplexer_1 (
    .in0(4'b0000), .in1(4'b0010), .out(multiplexer_1_out), .sel(is_LSL));
  Multiplexer #(.disabled("Z"), .width(4)) multiplexer_2 (
    .in0(multiplexer_1_out), .in1(4'b0011), .out(multiplexer_2_out), .sel(is_LSR));
  Multiplexer #(.disabled("Z"), .width(4)) multiplexer_3 (
    .in0(multiplexer_2_out), .in1(4'b0100), .out(multiplexer_3_out), .sel(is_ASR));
  Multiplexer #(.width(5)) multiplexer_4 (.in0({5{1'b0}}), .in1(imm5_field), .out(Imm5_On), .sel(is_shift));
  or or_1 (or_1_out, addsub_reg, addsub_imm3);
  or or_2 (or_2_out, addsub_reg, addsub_imm3);
  Multiplexer #(.disabled("Z"), .width(4)) multiplexer_5 (
    .in0(multiplexer_3_out), .in1(4'b1011), .out(multiplexer_5_out), .sel(is_add_any));
  Multiplexer #(.width(3)) multiplexer_6 (.in0(3'b000), .in1(rn_addsub), .out(multiplexer_6_out), .sel(or_1_out));
  Multiplexer #(.width(3)) multiplexer_7 (.in0(3'b000), .in1(rd_addsub), .out(multiplexer_7_out), .sel(or_2_out));
  Multiplexer #(.disabled("Z"), .width(4)) multiplexer_8 (
    .in0(multiplexer_5_out), .in1(4'b1010), .out(multiplexer_8_out), .sel(is_sub_any));
  Multiplexer #(.width(3)) multiplexer_9 (
    .in0(multiplexer_6_out), .in1(rdn), .out(multiplexer_9_out), .sel(addsub_imm8));
  Multiplexer #(.width(3)) multiplexer_10 (
    .in0(multiplexer_7_out), .in1(rdn), .out(multiplexer_10_out), .sel(addsub_imm8));
  Multiplexer #(.disabled("Z"), .width(4)) multiplexer_11 (
    .in0(multiplexer_8_out), .in1(4'b1000), .out(multiplexer_11_out), .sel(is_MOV_imm8));
  Multiplexer #(.disabled("Z"), .width(4)) multiplexer_12 (
    .in0(multiplexer_11_out), .in1(4'b1010), .out(ALU_Opcode_On), .sel(is_CMP_imm8));
  Multiplexer #(.width(3)) multiplexer_13 (
    .in0(multiplexer_9_out), .in1(rd_mov), .out(multiplexer_13_out), .sel(is_CMP_imm8));
  Multiplexer #(.width(3)) multiplexer_14 (
    .in0(multiplexer_10_out), .in1(rd_mov), .out(multiplexer_14_out), .sel(is_MOV_imm8));
  assign imm32_field = {{24{1'b0}}, imm8_field};  // Bit_Extender bit_extender_1
  Negator #(.width(32)) negator_1 (.in(imm32_field), .out(NEGimm32_field));
  Multiplexer #(.width(3)) multiplexer_15 (
    .in0(multiplexer_13_out), .in1(rm_shift), .out(multiplexer_15_out), .sel(is_shift));
  Multiplexer #(.width(3)) multiplexer_16 (
    .in0(multiplexer_14_out), .in1(rd_mov), .out(multiplexer_16_out), .sel(is_CMP_imm8));
  Multiplexer #(.width(3)) multiplexer_17 (.in0(multiplexer_15_out), .in1(rn_addsub), .out(Rn_On), .sel(addsub_reg));
  Multiplexer #(.width(3)) multiplexer_18 (.in0(multiplexer_16_out), .in1(rd_shift), .out(Rd_On), .sel(is_shift));
  assign bit_extender_2_out = {{29{1'b0}}, imm3_field};  // Bit_Extender bit_extender_2
  Multiplexer #(.width(3)) multiplexer_19 (.in0(3'b000), .in1(rm_shift), .out(multiplexer_19_out), .sel(is_shift));
  Multiplexer #(.width(32)) multiplexer_20 (
    .in0({32{1'b0}}), .in1(bit_extender_2_out), .out(multiplexer_20_out), .sel(addsub_imm3));
  Multiplexer #(.width(32)) multiplexer_21 (
    .in0(imm32_field), .in1(NEGimm32_field), .out(multiplexer_21_out), .sel(or_3_out));
  or or_3 (or_3_out, is_sub_any, is_CMP_imm8);
  Multiplexer #(.width(4)) multiplexer_22 (.in0(4'b0000), .in1(4'b1111), .out(m1), .sel(addsub));
  Multiplexer #(.width(4)) multiplexer_23 (.in0(m1), .in1(4'b1110), .out(m2), .sel(is_shift));
  Multiplexer #(.width(3)) multiplexer_24 (.in0(multiplexer_19_out), .in1(rm_addsub), .out(Rm_On), .sel(addsub_reg));
  Multiplexer #(.width(32)) multiplexer_25 (
    .in0(multiplexer_20_out), .in1(multiplexer_21_out), .out(multiplexer_25_out), .sel(is_imm8_any));
  Multiplexer #(.width(32)) multiplexer_26 (
    .in0({32{1'b0}}), .in1(multiplexer_25_out), .out(Imm32_On), .sel(is_imm_any));
  Multiplexer #(.width(4)) multiplexer_27 (.in0(m2), .in1(4'b1100), .out(m3), .sel(is_MOV_imm8));
  Multiplexer #(.width(4)) multiplexer_28 (.in0(m3), .in1(4'b1111), .out(Flag_Update_Mask_On), .sel(is_CMP_imm8));

  assign Carry_On = is_sub_any;
  assign Imm32_Enable_On = is_imm_any;

  // Other names for the same wires on the sheet: is_addsub = addsub; is_addsub_imm3 = addsub_imm3;
  //   is_addsub_imm8 = addsub_imm8; is_addsub_reg = addsub_reg
endmodule

module EnableGate (
  input  Imm32_Enable_On,
  input  [31:0] Imm32_On,
  input  [3:0] ALU_Opcode_On,
  input  [2:0] Rm_On,
  input  [2:0] Rn_On,
  input  [2:0] Rd_On,
  input  Carry_On,
  input  [4:0] Imm5_On,
  input  [3:0] Flag_Update_Mask_On,
  input  Enable,
  output [31:0] Imm32,
  output [2:0] Rn,
  output [3:0] ALU_Opcode,
  output [3:0] Flag_Update_Mask,
  output [2:0] Rm,
  output [2:0] Rd,
  output [4:0] Imm5,
  output Carry,
  output Imm32_Enable
);

  Multiplexer multiplexer_1 (.in0(1'b0), .in1(Imm32_Enable_On), .out(Imm32_Enable), .sel(Enable));
  Multiplexer #(.width(3)) multiplexer_2 (.in0(3'b000), .in1(Rm_On), .out(Rm), .sel(Enable));
  Multiplexer #(.disabled("Z"), .width(3)) multiplexer_3 (.in0(3'b000), .in1(Rd_On), .out(Rd), .sel(Enable));
  Multiplexer #(.width(32)) multiplexer_4 (.in0({32{1'b0}}), .in1(Imm32_On), .out(Imm32), .sel(Enable));
  Multiplexer #(.disabled("Z"), .width(5)) multiplexer_5 (.in0({5{1'b0}}), .in1(Imm5_On), .out(Imm5), .sel(Enable));
  Multiplexer #(.disabled("Z")) multiplexer_6 (.in0(1'b0), .in1(Carry_On), .out(Carry), .sel(Enable));
  Multiplexer #(.disabled("Z"), .width(3)) multiplexer_7 (.in0(3'b000), .in1(Rn_On), .out(Rn), .sel(Enable));
  Multiplexer #(.disabled("Z"), .width(4)) multiplexer_8 (
    .in0(4'b0000), .in1(ALU_Opcode_On), .out(ALU_Opcode), .sel(Enable));
  Multiplexer #(.disabled("Z"), .width(4)) multiplexer_9 (
    .in0(4'b0000), .in1(Flag_Update_Mask_On), .out(Flag_Update_Mask), .sel(Enable));
endmodule
