// Logisim project Ctl_Data_Processing.circ as structural Verilog: 1 circuit, main circuit Data_Processing
module Data_Processing (
  input  Enable,
  input  [15:0] Instruction,
  output [2:0] Rd,
  output [2:0] Rn,
  output [2:0] Rm,
  output [3:0] ALU_Opcode,
  output [3:0] Flags_Update_Mask
);

  wire enable_ok, isDP, isMUL, isRSB, swapRn;
  wire [2:0] decoded_Rm, decoded_Rn;
  wire [3:0] rom_1_data;

  Comparator #(.width(6)) comparator_1 (.a(Instruction[15:10]), .b(6'b010000), .eq(isDP));  // open: gt, lt
  and and_1 (enable_ok, Enable, isDP);
  Multiplexer #(.width(4)) multiplexer_1 (.in0(4'b0000), .in1(Instruction[9:6]), .out(ALU_Opcode), .sel(enable_ok));
  Comparator #(.width(4)) comparator_2 (.a(Instruction[9:6]), .b(4'b1101), .eq(isMUL));  // open: gt, lt
  Comparator #(.width(4)) comparator_3 (.a(Instruction[9:6]), .b(4'b1001), .eq(isRSB));  // open: gt, lt
  or or_1 (swapRn, isRSB, isMUL);
  ROM #(.addrWidth(4), .dataWidth(4)) rom_1 (.addr(Instruction[9:6]), .data(rom_1_data));
  Multiplexer #(.width(3)) multiplexer_2 (
    .in0(Instruction[5:3]), .in1(Instruction[2:0]), .out(decoded_Rm), .sel(isMUL));
  Multiplexer #(.width(3)) multiplexer_3 (
    .in0(Instruction[2:0]), .in1(Instruction[5:3]), .out(decoded_Rn), .sel(swapRn));
  Multiplexer #(.width(3)) multiplexer_4 (.in0(3'b000), .in1(decoded_Rm), .out(Rm), .sel(enable_ok));
  Multiplexer #(.width(3)) multiplexer_5 (.in0(3'b000), .in1(decoded_Rn), .out(Rn), .sel(enable_ok));
  Multiplexer #(.width(3)) multiplexer_6 (.in0(3'b000), .in1(Instruction[2:0]), .out(Rd), .sel(enable_ok));
  Multiplexer #(.width(4)) multiplexer_7 (.in0(4'b0000), .in1(rom_1_data), .out(Flags_Update_Mask), .sel(enable_ok));

  // Other names for the same wires on the sheet: decoded_Rd[2:0] = Instruction[2:0]; Rdn[2:0] = Instruction[2:0];
  //   RmField[2:0] = Instruction[5:3]; ALUop[3:0] = Instruction[9:6]; Prefix[5:0] = Instruction[15:10]

  // Notes on the sheet:
  //   contents of rom_1 (hex, n*v repeats v):
  //   5*e f f e e f f f e c e e
  //   Pull output low on Enable = 0
endmodule
