// Logisim project Ctl_Flags_APSR.circ as structural Verilog: 1 circuit, main circuit Flags_APSR
module Flags_APSR (
  input  [3:0] Update_Mask,
  input  [3:0] Flags_In,
  input  Clk,
  input  Rst,
  output [3:0] Flags_Out
);

  wire [3:0] EXIT_4bits;

  Multiplexer multiplexer_1 (.in0(Flags_Out[0]), .in1(Flags_In[0]), .out(EXIT_4bits[0]), .sel(Update_Mask[0]));
  Multiplexer multiplexer_2 (.in0(Flags_Out[1]), .in1(Flags_In[1]), .out(EXIT_4bits[1]), .sel(Update_Mask[1]));
  Register #(.width(4)) register_1 (.D(EXIT_4bits), .en(1'b1), .clk(Clk), .Q(Flags_Out), .clr(Rst));
  Multiplexer multiplexer_3 (.in0(Flags_Out[2]), .in1(Flags_In[2]), .out(EXIT_4bits[2]), .sel(Update_Mask[2]));
  Multiplexer multiplexer_4 (.in0(Flags_Out[3]), .in1(Flags_In[3]), .out(EXIT_4bits[3]), .sel(Update_Mask[3]));

  // Other names for the same wires on the sheet: EXIT_ZERO = EXIT_4bits[0]; EXIT_UN = EXIT_4bits[1];
  //   EXIT_DEUX = EXIT_4bits[2]; EXIT_TROIS = EXIT_4bits[3]; ZERO_IN = Flags_In[0]; UN_IN = Flags_In[1];
  //   DEUX_IN = Flags_In[2]; TROIS_IN = Flags_In[3]; ZERO_OUT = Flags_Out[0]; UN_OUT = Flags_Out[1];
  //   DEUX_OUT = Flags_Out[2]; TROIS_OUT = Flags_Out[3]; ZERO = Update_Mask[0]; UN = Update_Mask[1];
  //   DEUX = Update_Mask[2]; TROIS = Update_Mask[3]
endmodule
