// Logisim project Ctl_Load_Store.circ as structural Verilog: 1 circuit, main circuit Load_Store
module Load_Store (
  input  [15:0] Instruction,
  input  Clk,
  input  Reset,
  input  [31:0] Stack_Pointer,
  input  Enable,
  output Store,
  output Load,
  output PC_Hold,
  output [2:0] Rmd,
  output [31:0] RAM_Addr
);

  wire comparator_2_eq, Load_decode, load_req, mem, mem_prev, not_mem_prev, or_1_out;
  wire [31:0] addr_raw, imm32;

  Adder #(.width(32)) adder_1 (.a(Stack_Pointer), .b(imm32), .out(addr_raw));  // open: cin, cout
  assign imm32 = {{24{Instruction[7]}}, Instruction[7:0]};  // Bit_Extender bit_extender_1
  Multiplexer #(.width(32)) multiplexer_1 (.in0({32{1'b0}}), .in1(addr_raw), .out(RAM_Addr), .sel(Enable));
  Comparator #(.width(4)) comparator_1 (.a(Instruction[3:0]), .b(4'b1001), .eq(Load_decode));  // open: gt, lt
  Comparator #(.width(4)) comparator_2 (.a(Instruction[3:0]), .b(4'b0010), .eq(comparator_2_eq));  // open: gt, lt
  and and_1 (load_req, Load_decode, PC_Hold);
  or or_1 (or_1_out, Load_decode, comparator_2_eq);
  and and_2 (mem, or_1_out, Enable);
  and and_3 (Store, Enable, Instruction[11]);
  Register #(.width(1)) Register_Load (.D(load_req), .en(1'b1), .clk(Clk), .Q(Load), .clr(Reset));
  Register #(.width(1)) register_1 (.D(mem), .en(1'b1), .clk(Clk), .Q(mem_prev), .clr(Reset));
  not not_1 (not_mem_prev, mem_prev);
  and and_4 (PC_Hold, mem, not_mem_prev);

  assign Rmd = Instruction[10:8];

  // Other names for the same wires on the sheet: imm8[7:0] = Instruction[7:0]; instruction_11 = Instruction[11];
  //   mem_pulse = PC_Hold

  // Notes on the sheet:
  //   Delay load and hold PC for 1 cycle for the RAM to send out requested data 
endmodule
