// Logisim project Ctl_SP_Address.circ as structural Verilog: 1 circuit, main circuit SP_Address
module SP_Address (
  input  [31:0] Stack_Pointer,
  input  [15:0] Instruction,
  input  Enable,
  output [31:0] New_Stack_Pointer,
  output Write_Enable
);

  wire is_sp_addsub, m1, m2;
  wire [31:0] imm32, sp_calc, sp_minus, sp_plus;

  and and_1 (is_sp_addsub, m1, m2);
  Adder #(.width(32)) adder_1 (.a(Stack_Pointer), .b(imm32), .out(sp_plus));  // open: cin, cout
  Comparator #(.width(4)) comparator_1 (.a(4'b1011), .b(Instruction[15:12]), .eq(m1));  // open: gt, lt
  Comparator #(.width(4)) comparator_2 (.a(4'b0000), .b(Instruction[11:8]), .eq(m2));  // open: gt, lt
  and and_2 (Write_Enable, Enable, is_sp_addsub);
  Subtractor #(.width(32)) subtractor_1 (.a(Stack_Pointer), .b(imm32), .out(sp_minus));  // open: bin, bout
  Multiplexer #(.width(32)) multiplexer_1 (.in0(sp_plus), .in1(sp_minus), .out(sp_calc), .sel(Instruction[7]));
  Multiplexer #(.width(32)) multiplexer_2 (
    .in0({32{1'b0}}), .in1(sp_calc), .out(New_Stack_Pointer), .sel(Write_Enable));
  assign imm32 = {{25{1'b0}}, Instruction[6:0]};  // Bit_Extender bit_extender_1

  // Other names for the same wires on the sheet: Active = Write_Enable; imm7[6:0] = Instruction[6:0];
  //   sub = Instruction[7]; offset32[31:0] = imm32

  // Notes on the sheet:
  //   Pull output low on Enable = 0
endmodule
